# Fritzing sketch heater (saved by Fritzing 0.9.3b)
breadboards: 1

parts:
  U1 = ESP32S-HiLetgo [part_number=ESP32S-HiLetgo]
  Mod2 = KY-019 5V Relay Module [package="Breakout board"]
  R1 = Heating Pad

nets:
  N1: U1.3.3, Mod2.+, Mod2.Common
  N2: U1.GND, Mod2.-, R1.pin_1
  N3: U1.GPIO17, Mod2.S
  N4: Mod2.NO, R1.pin_0

custom parts:
  ESP32S-HiLetgo: HiLetgo ESP-WROOM-32 ESP32 ESP-32S Development Board 2.4GHz Dual-Mode WiFi + Bluetooth Dual Cores Microcontroller The ESP32 integrated with Antenna switches, RF Balun, power amplifiers, low-noise amplifiers, filters, and management modules, and the entire solution occupies the least area of PCB. 2.4 GHz Wi-Fi plus Bluetooth dual-mode chip, with TSMC Ultra-low power consumption 40nm technology,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
  KY-019 5V Relay Module: KY-019 5V Relay module, used to control AC circuits. (Special thanks to vanepp for fixing the PCB holes and other errors)
  Heating Pad: A thermoresistant material with an embeded conductor that dissipates electrical energy into heat.
