# Fritzing sketch led_fan (saved by Fritzing 0.9.3b)
breadboards: 1

parts:
  Mod1 = KY-019 5V Relay Module [package="Breakout board"]
  Power_plug1 = Power plug
  U1 = ESP32S-HiLetgo [part_number=ESP32S-HiLetgo]
  F1 = Fan - Ventilador [package=THT]
  Mod2 = KY-019 5V Relay Module [package="Breakout board"]
  LED1 = smd LED [color="Red (633nm)" package="0805 [SMD]"]

nets:
  GND: Mod1.S, Mod1.-, U1.GND, F1.GND, Mod2.-
  N1: Mod1.+, U1.3.3, Mod2.+, Mod2.Common
  N2: Mod1.Common, Power_plug1.VCC
  N3: Mod1.NO, LED1.anode
  N4: Power_plug1.GND, LED1.cathode
  N5: U1.GPIO17, Mod2.S
  N6: F1.5V, Mod2.NO

custom parts:
  KY-019 5V Relay Module: KY-019 5V Relay module, used to control AC circuits. (Special thanks to vanepp for fixing the PCB holes and other errors)
  ESP32S-HiLetgo: HiLetgo ESP-WROOM-32 ESP32 ESP-32S Development Board 2.4GHz Dual-Mode WiFi + Bluetooth Dual Cores Microcontroller The ESP32 integrated with Antenna switches, RF Balun, power amplifiers, low-noise amplifiers, filters, and management modules, and the entire solution occupies the least area of PCB. 2.4 GHz Wi-Fi plus Bluetooth dual-mode chip, with TSMC Ultra-low power consumption 40nm technology,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
  Fan - Ventilador: Ventilador de 2 pines, se encuentra comunmente en computadoras de escritorio
