# Fritzing sketch sensor_control (saved by Fritzing 0.9.3b)
breadboards: 1

parts:
  Water_Level_Sensor1 = Water Level Sensor
  U1 = ESP32S-HiLetgo [part_number=ESP32S-HiLetgo]
  U2 = L9110 H-bridge module [part_number="L9110 H-bridge"]
  WATER_PUMP1 = water pump/motor  # not connected

nets:
  N1: Water_Level_Sensor1.SIG, U1.GPIO27
  VCC: Water_Level_Sensor1.VCC, U1.GPIO7, U2.VCC
  GND: Water_Level_Sensor1.GND, U1.GPIO6, U2.GND
  N2: U1.GPIO35, U2.B-IB
  N3: U1.GPIO26, U2.B-IA

custom parts:
  Water Level Sensor: A water level sensor. This sensor operates at 3V to 5V. The Sig (signal) pin outputs an analogue signal that is in proportion to the amount of water in contact with the sensor.
  ESP32S-HiLetgo: HiLetgo ESP-WROOM-32 ESP32 ESP-32S Development Board 2.4GHz Dual-Mode WiFi + Bluetooth Dual Cores Microcontroller The ESP32 integrated with Antenna switches, RF Balun, power amplifiers, low-noise amplifiers, filters, and management modules, and the entire solution occupies the least area of PCB. 2.4 GHz Wi-Fi plus Bluetooth dual-mode chip, with TSMC Ultra-low power consumption 40nm technology,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
  water pump/motor: WATER PUMP BY ARDUBLOCKTR
